# Fritzing sketch 00_LED+Button (saved by Fritzing 0.7.5b)
breadboards: 1

parts:
  LED1 = LED - 5mm [color="Red (633nm)" package="5 mm [THT]"]
  R1 = Resistor [tolerance=±5% resistance=220 package=THT]
  Arduino1 = Arduino
  S1 = Pushbutton [package=THT]

nets:
  GND: LED1.cathode, Arduino1.GND
  N1: LED1.anode, R1.Pin_1
  N2: R1.Pin_0, S1.leg0
  5V: Arduino1.+5V, S1.leg1
