# Fritzing sketch 01_blink (saved by Fritzing 0.7.5b)
breadboards: 1

parts:
  Arduino1 = Arduino
  LED1 = LED - 5mm [color="Red (633nm)" package="5 mm [THT]"]
  R1 = Resistor [tolerance=±5% resistance=220 package=THT]

nets:
  GND: Arduino1.GND, LED1.cathode
  N1: Arduino1.D11, R1.Pin_0
  N2: LED1.anode, R1.Pin_1
