# Fritzing sketch 02_pushButton+LED (saved by Fritzing 0.7.5b)
breadboards: 1

parts:
  Arduino1 = Arduino
  LED1 = LED - 5mm [color="Red (633nm)" package="5 mm [THT]"]
  R1 = Resistor [tolerance=±5% resistance=220 package=THT]
  R2 = Resistor [tolerance=±5% resistance=1k package=THT]
  S1 = Pushbutton [package=THT]

nets (from the breadboard view):
  N1: Arduino1.GND, LED1.cathode, R2.Pin_0
  N2: Arduino1.D11, R1.Pin_0
  N3: Arduino1.D2, R2.Pin_1, S1.leg0
  N4: Arduino1.+5V, S1.leg1
  N5: LED1.anode, R1.Pin_1
