# Fritzing sketch LDR_input (saved by Fritzing 0.7.5b)
breadboards: 1

parts:
  Arduino1 = Arduino
  R1 = Resistor [tolerance=±5% resistance=220 package=THT]
  R4 = Resistor [tolerance=±5% resistance=1k package=THT]
  R5 = Photocell (LDR) [package=THT]
  LED1 = LED - 5mm [color="Red (633nm)" package="5 mm [THT]"]

nets:
  GND: Arduino1.GND, R4.Pin_1, LED1.cathode
  N1: Arduino1.D11, R1.Pin_0
  5V: Arduino1.+5V, R5.pin_0
  N2: Arduino1.A0, R4.Pin_0, R5.pin_1
  N3: R1.Pin_1, LED1.anode
